# Fritzing sketch Circuit_Diagram (saved by Fritzing 1.0.6)

parts:
  U1 = ESP32S-HiLetgo [part_number=ESP32S-HiLetgo]
  Bat1 = battery_holder_single_18650  # not connected
  Bat2 = battery_holder_single_18650
  J1 = XL4015 DC-DC CC CV module (blue)  # not connected
  Part1 = Adafruit PCA9685 PWM/Servo Breakout [part_number=815]
  C1 = Capacitor Polarized [package=cpol-radial-10uf-25v]
  C2 = Capacitor Polarized [package=panasonic_h13]  # not connected
  S1 = Rocker Switch

nets:
  N1: U1.GPIO11, C1.-
  N2: U1.VIN, C1.+
  N3: U1.GPIO6, Part1.VCC
  N4: U1.GPIO7, Part1.GND
  N5: U1.GPIO3, Part1.SCL
  N6: U1.GPIO23, Part1.SDA
  N7: Bat2.+, S1.pin_1

custom parts:
  ESP32S-HiLetgo: HiLetgo ESP-WROOM-32 ESP32 ESP-32S Development Board 2.4GHz Dual-Mode WiFi + Bluetooth Dual Cores Microcontroller The ESP32 integrated with Antenna switches, RF Balun, power amplifiers, low-noise amplifiers, filters, and management modules, and the entire solution occupies the least area of PCB. 2.4 GHz Wi-Fi plus Bluetooth dual-mode chip, with TSMC Ultra-low power consumption 40nm technology,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
  battery_holder_single_18650: single 18650 battery holder
  XL4015 DC-DC CC CV module (blue): XL4015 DC-DC CC/CV module blue
  Adafruit PCA9685 PWM/Servo Breakout: Using only two pins, control 16 free-running PWM outputs! I2C-controlled PWM driver with a built in clock. Unlike the TLC5940 family, you do not need to continuously send it signal tying up your microcontroller, its completely free running! 5V compliant, which means you can control it from a 3.3V microcontroller and still safely drive up to 6V outputs (this is good for when you want to control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
